# Fritzing sketch nodemcu (saved by Fritzing 0.9.3b)

parts:
  U1 = ESP8266 NodeMCU LoLin module
  S1 = H-Bridge with L298N
  M1 = DC Motor
  M2 = DC Motor
  BAT1 = BC9VPC [package=bc9vpc]

nets:
  N1: U1.D1, S1.IN4
  N2: U1.D2, S1.IN3
  N3: U1.D3, S1.IN2
  N4: U1.D4, S1.IN1
  3V3: U1.3V3, S1.5V
  N5: S1.12V, BAT1.V+
  N6: S1.GND, BAT1.V-
  N7: S1.M1-01, M2.pin_2
  N8: S1.M1-02, M2.pin_1
  N9: S1.M2-01, S1.M2-02, M1.pin_1, M1.pin_2

custom parts:
  ESP8266 NodeMCU LoLin module: ESP8266 based NodeMCU
  H-Bridge with L298N: h-bridge
